# Fritzing sketch mike_MkI (saved by Fritzing 0.9.0b)
circuit board: 8.46667cm x 5.64444cm
breadboards: 1

parts:
  Part2 = Arduino Uno (Rev3)  # not connected
  M1 = DC Motor
  M2 = DC Motor
  S1 = Pushbutton [package="[THT]"]
  LED1 = LED - 5mm [color="Red (633nm)" package="5 mm [THT]"]
  LCD2 = LCD screen
  Part3 = SRF05 Ultrasonic Rangefinder
  R2 = Resistor [tolerance=±5% resistance=220 package=THT]
  R1 = Trimmer Potentiometer [maximum_resistance=10kΩ package=THT]
  Part1 = Arduino Motor Shield (Rev3)

nets:
  N1: M1.pin_1, Part1.A+
  N2: M1.pin_2, Part1.A-
  N3: M2.pin_1, Part1.B+
  N4: M2.pin_2, Part1.B-
  N5: S1.Pin_1, S1.Pin_2, Part1.A1
  GND: S1.Pin_3, S1.Pin_4, LED1.cathode, LCD2.VSS, LCD2.R/W, Part3.GND, R1.leg1, Part1.GND
  N6: LED1.anode, R2.Pin_1
  VDD: LCD2.VDD, LCD2.LED+, LCD2.LED-, Part3.VCC, R1.leg2, Part1.5V
  N7: LCD2.V0, R1.wiper
  N8: LCD2.RS, Part1.D5_PWM
  N9: LCD2.E, Part1.D6_PWM
  N10: LCD2.DB4, Part1.IOREF
  N11: LCD2.DB5, Part1.D1/TX
  N12: LCD2.DB6, Part1.D2
  N13: LCD2.DB7, Part1.D4
  N14: Part3.Trig, Part1.D10_PWM
  N15: Part3.Echo, Part1.D7
  N16: R2.Pin_0, Part1.A0

notes:
  16
  1
